// Logisim project dfhjdhf.circ as structural Verilog: 1 circuit, main circuit main
module main (
  input  in_1,
  output out_2,
  output out_3,
  output out_4
);

  wire and_1_out, clock_1_out, j_k_ff_1_qn, j_k_ff_3_qn;

  Clock clock_1 (.out(clock_1_out));
  J_K_Flip_Flop j_k_ff_1 (
    .J(and_1_out), .clk(clock_1_out), .K(out_4), .Q(out_2), .Qn(j_k_ff_1_qn));  // open: preset, en, reset
  J_K_Flip_Flop j_k_ff_2 (.J(in_1), .clk(clock_1_out), .K(j_k_ff_1_qn), .Q(out_4));  // open: Qn, preset, en, reset
  and and_1 (and_1_out, out_4, j_k_ff_3_qn);
  J_K_Flip_Flop j_k_ff_3 (
    .J(out_2), .clk(clock_1_out), .K(j_k_ff_1_qn), .Q(out_3), .Qn(j_k_ff_3_qn));  // open: preset, en, reset
endmodule
